# Fritzing sketch IR (saved by Fritzing 1.0.5)
breadboards: 1

parts:
  M1 = fc-51 [package=THT]
  Part1 = Arduino Uno (Rev3)
  LED1 = LED - 5mm [color="Red (633nm)" current=0.030A package="5 mm [THT]"]

nets:
  N1: M1.pin1, Part1.A0
  N2: M1.pin2, Part1.GND, LED1.cathode
  N3: M1.pin3, Part1.5V
  N4: Part1.D13/SCK, LED1.anode
