# Fritzing sketch MQ9 (saved by Fritzing 1.0.5)
breadboards: 1

parts:
  Part1 = Arduino Uno (Rev3)
  Part2 = MQ-9 breakout
  LED1 = LED - 5mm [color="Red (633nm)" current=0.030A package="5 mm [THT]"]

nets:
  N1: Part1.A0, Part2.AO
  N2: Part1.D13/SCK, LED1.anode
  5V: Part1.5V, Part2.VCC
  GND: Part1.GND, Part2.GND, LED1.cathode

custom parts:
  MQ-9 breakout: SKU: 101284
