# Fritzing sketch interrupt (saved by Fritzing 1.0.5)
breadboards: 1

parts:
  S1 = Momentary Switch [package=ksa_sealed_tac_switch]
  LED1 = LED - 5mm [color="Red (633nm)" current=0.030A package="5 mm [THT]"]
  Part1 = Arduino Uno (Rev3)

nets:
  N1: S1.1, Part1.D2
  N2: S1.4, LED1.cathode, Part1.GND
  N3: LED1.anode, Part1.D13/SCK
